// Logisim project logisim.circ as structural Verilog: 1 circuit, main circuit main
module main (
  input  in_1,
  input  [7:0] in_2,
  input  [7:0] in_3,
  input  [7:0] in_4,
  output [15:0] out_5,
  output [15:0] out_6,
  output [15:0] out_7,
  output [15:0] out_8,
  output [15:0] out_9,
  output [15:0] out_10,
  output [15:0] out_11,
  output [15:0] out_12
);

  wire clock_1_out;

  Clock clock_1 (.out(clock_1_out));
  Shifter #(.width(16)) shifter_1 (.in({in_2, in_3}), .\dist ({4{in_1}}), .out(out_5));
  Shifter #(.width(16)) shifter_2 (.in({in_2, in_3}), .\dist ({{3{in_1}}, in_4[1]}), .out(out_6));
  Shifter #(.width(16)) shifter_3 (.in({in_2, in_3}), .\dist ({{2{in_1}}, in_4[2], in_1}), .out(out_7));
  Shifter #(.width(16)) shifter_4 (.in({in_2, in_3}), .\dist ({{2{in_1}}, {2{in_4[3]}}}), .out(out_8));
  Shifter #(.width(16)) shifter_5 (.in({in_2, in_3}), .\dist ({in_1, in_4[4], {2{in_1}}}), .out(out_9));
  Shifter #(.width(16)) shifter_6 (.in({in_2, in_3}), .\dist ({in_1, in_4[5], in_1, in_4[5]}), .out(out_10));
  Shifter #(.width(16)) shifter_7 (.in({in_2, in_3}), .\dist ({in_1, {2{in_4[6]}}, in_1}), .out(out_11));
  Shifter #(.width(16)) shifter_8 (.in({in_2, in_3}), .\dist ({in_1, {3{in_4[7]}}}), .out(out_12));
  Adder adder_1 ();  // open: a, b, out, cin, cout
endmodule
